// Logisim project DECODER 3 X 8.circ as structural Verilog: 1 circuit, main circuit main
module main (
  input  A,
  input  B,
  input  C,
  output S0,
  output S1,
  output S2
);

  wire not_1_out, not_2_out, not_3_out, not_4_out, not_5_out, not_6_out, not_7_out;

  not not_1 (not_1_out, A);
  not not_2 (not_2_out, A);
  not not_3 (not_3_out, A);
  not not_4 (not_4_out, B);
  not not_5 (not_5_out, B);
  not not_6 (not_6_out, C);
  not not_7 (not_7_out, C);
  and and_1 (S0, not_1_out, not_4_out, not_6_out);
  and and_2 (S1, not_2_out, not_5_out, C);
  and and_3 (S2, not_3_out, B, not_7_out);
endmodule
